// Logisim project FINAL CPE 142 Assignment 11 Jimenez.circ as structural Verilog: 1 circuit, main circuit main
module main (
);

  wire _3, _6, _7, and_1_out, Clear, CLK, Clock, clock_1_out, comparator_1_eq, decoder_1_out1,
       decoder_1_out2, decoder_1_out4, decoder_1_out5, not_1_out, not_2_out, or_1_out, Reset,
       stallablememory_1_p9;
  wire [7:0] adder_1_out, counter_1_q, multiplexer_1_out, multiplexer_2_out, ram_1_data, register_1_q,
       stallablememory_1_p1, stallablememory_1_p7;
  wire [15:0] assoccache16bit_1_data_out;

  not not_1 (not_1_out, comparator_1_eq);
  and and_1 (and_1_out, not_1_out, decoder_1_out2);
  Counter counter_1 (
    .load(and_1_out), .D(adder_1_out), .count(not_2_out), .Q(counter_1_q), .clk(Clock), .clr(Reset));  // open: carry
  not not_2 (not_2_out, and_1_out);
  Button button_1 (.out(Reset));
  Button button_2 (.out(Clear));
  AssocCache16bit assoccache16bit_1 (
    .address(counter_1_q), .Clear(Clear), .Clock(clock_1_out), .data_out(assoccache16bit_1_data_out),
    .Stallable_Clock(CLK));
  Clock clock_1 (.out(clock_1_out));
  Adder adder_1 (.a(counter_1_q), .b(assoccache16bit_1_data_out[15:8]), .out(adder_1_out));  // open: cin, cout
  Decoder #(.select(3), .enable("false")) decoder_1 (
    .out1(decoder_1_out1), .out2(decoder_1_out2), .out3(_3), .out4(decoder_1_out4), .out5(decoder_1_out5),
    .out6(_6), .out7(_7), .sel(assoccache16bit_1_data_out[2:0]));  // open: out0
  Register register_1 (.D(multiplexer_2_out), .en(or_1_out), .Q(register_1_q), .clk(Clock), .clr(Clear));
  or or_1 (or_1_out, decoder_1_out4, _6, _3);
  // StallableMemory stallablememory_1: pin names not known; wires that end beside it: stallablememory_1_p1, register_1_q, _7, CLK, _6, Reset, stallablememory_1_p7, Clock, stallablememory_1_p9
  RAM #(.addrWidth(3), .bus("separate")) ram_1 (
    .addr(assoccache16bit_1_data_out[5:3]), .din(register_1_q), .data(ram_1_data), .str(decoder_1_out5),
    .clk(Clock), .ld(1'b1), .clr(Clear));  // open: sel
  Multiplexer #(.width(8), .enable("false")) multiplexer_1 (
    .in0(assoccache16bit_1_data_out[15:8]), .in1(register_1_q), .out(multiplexer_1_out), .sel(_3));
  TTY tty_1 (.data(register_1_q[6:0]), .clk(Clock), .we(decoder_1_out1), .clr(Reset));
  LED led_1 (.in(stallablememory_1_p9));
  Adder adder_2 (.a(multiplexer_1_out), .b(ram_1_data), .out(stallablememory_1_p1));  // open: cin, cout
  Multiplexer #(.width(8), .enable("false")) multiplexer_2 (
    .in0(stallablememory_1_p1), .in1(stallablememory_1_p7), .out(multiplexer_2_out), .sel(_6));
  Hex_Digit_Display hex_digit_display_1 (.value(register_1_q[3:0]));  // open: dp
  Hex_Digit_Display hex_digit_display_2 (.value(register_1_q[7:4]));  // open: dp
  Comparator comparator_1 (.a(ram_1_data), .b(register_1_q), .eq(comparator_1_eq));  // open: gt, lt

  // Notes on the sheet:
  //   Instruction RAM
  //   ACCU
  //   Stall_Mem (Data RAM)
  //    Register File
  //   ALU
endmodule
