// Logisim project connectable_instruction_cache (1).circ as structural Verilog: 2 circuits, main circuit AssocCache16bit
module AssocCache16bit (
  input  [7:0] address,
  input  Clear,
  input  Clock,
  output [15:0] data_out,
  output Stallable_Clock
);

  wire and_1_out, and_2_out, comparator_1_eq, comparator_2_eq, hit, LRU0, LRU1, nextlevelcache_1_stalled,
       not_2_out, not_4_out, or_2_out;
  wire [1:0] ram_2_data;
  wire [1:1] and_3_out;
  wire [3:0] bit_extender_1_out, bit_extender_2_out;
  wire [4:0] ram_2_data_2;
  wire [15:0] mem_data, ram_2_data_3;
  wire [22:21] ram_2_data_4;
  wire [22:22] not_1_out;
  wire [23:0] multiplexer_1_out, multiplexer_2_out, ram_1_data;

  RAM #(.addrWidth(3), .dataWidth(24), .bus("separate")) ram_1 (
    .addr(address[2:0]), .din(multiplexer_1_out), .data(ram_1_data), .str(or_2_out), .sel(1'b1), .clk(Clock),
    .ld(1'b1), .clr(Clear));
  Comparator #(.width(5)) comparator_1 (.a(ram_1_data[4:0]), .b(address[7:3]), .eq(comparator_1_eq));  // open: gt, lt
  Multiplexer #(.width(24), .enable("false")) multiplexer_1 (
    .in0({1'b0, not_1_out[22], ram_1_data[21:0]}), .in1({3'b001, mem_data, address[7:3]}),
    .out(multiplexer_1_out), .sel(LRU0));
  not not_1 (not_1_out[22], and_1_out);
  and and_1 (and_1_out, ram_1_data[21], comparator_1_eq);
  LED led_1 (.in(and_1_out));
  or or_1 (hit, and_2_out, and_1_out);
  or or_2 (or_2_out, and_3_out[1], hit);
  NextLevelCache nextlevelcache_1 (
    .Address(address), .store(1'b0), .clock(Clock), .select(not_2_out), .clear(Clear), .data_out(mem_data),
    .stalleable_clock(Stallable_Clock), .Stalled(nextlevelcache_1_stalled));  // open: data_in
  assign bit_extender_1_out = {{2{1'b0}}, ram_1_data[23:22]};  // Bit_Extender bit_extender_1
  assign bit_extender_2_out = {{2{1'b0}}, ram_2_data};  // Bit_Extender bit_extender_2
  Hex_Digit_Display hex_digit_display_1 (.value(bit_extender_1_out));  // open: dp
  Hex_Digit_Display hex_digit_display_2 (.value(bit_extender_2_out));  // open: dp
  RAM #(.addrWidth(3), .dataWidth(24), .bus("separate")) ram_2 (
    .addr(address[2:0]), .din(multiplexer_2_out),
    .data({ram_2_data, ram_2_data_4[21], ram_2_data_3, ram_2_data_2}), .str(or_2_out), .clk(Clock),
    .ld(1'b1), .clr(Clear));  // open: sel
  Comparator #(.width(5)) comparator_2 (.a(ram_2_data_2), .b(address[7:3]), .eq(comparator_2_eq));  // open: gt, lt
  not not_2 (not_2_out, hit);
  Multiplexer #(.width(24), .enable("false")) multiplexer_2 (
    .in0({1'b0, ram_2_data_4, ram_2_data_3, ram_2_data_2}), .in1({3'b001, mem_data, address[7:3]}),
    .out(multiplexer_2_out), .sel(LRU1));
  and and_2 (and_2_out, ram_2_data_4[21], comparator_2_eq);
  not not_3 (ram_2_data_4[22], and_2_out);
  LED led_2 (.in(and_2_out));
  not not_4 (not_4_out, nextlevelcache_1_stalled);
  nor nor_1 (LRU0, hit, 1'b0);
  nor nor_2 (LRU1, hit, 1'b1);
  LED led_3 (.in(or_2_out));
  LED led_4 (.in(and_3_out[1]));
  and and_3 (and_3_out[1], not_2_out, not_4_out);
  Multiplexer #(.select(2), .width(16)) multiplexer_3 (
    .in0(ram_2_data_3), .in1(ram_1_data[20:5]), .in2(mem_data), .in3(mem_data), .out(data_out),
    .sel({and_3_out[1], ram_2_data_4[22]}), .en(or_2_out));
  Hex_Digit_Display hex_digit_display_3 (.value(data_out[15:12]));  // open: dp
  Hex_Digit_Display hex_digit_display_4 (.value(data_out[11:8]));  // open: dp

  // Other names for the same wires on the sheet: clr = Clear; missed_line[20:0] = {mem_data, address[7:3]};
  //   req_tag[4:0] = address[7:3]

  // Notes on the sheet:
  //   input address from CPU [disconnected]
  //   0-4: tag
  //   5-20: data
  //   21: valid
  //   22-23: LRU
  //   Way0
  //   set 0 hit
  //   Way1
  //   NextLevelCache
  //   Way0 Age 
  //   Way1 Age 
  //   How to connect way ages to LRU0 and LRU1 so oldest way is selected for replacement? 
  //   set 1 hit
  //   return data ready
  //   Form a new line to fill cache with data, tag, valid bit and LRU set to zero
  //   Return Data to CPU
  //   data return from main mem
endmodule

module NextLevelCache (
  input  [7:0] Address,
  input  [15:0] data_in,
  input  store,
  input  clear,
  input  select,
  input  clock,
  output [15:0] data_out,
  output stalleable_clock,
  output Stalled
);

  wire counter_1_carry, or_1_out;
  wire [3:0] counter_1_q;

  or or_1 (or_1_out, store, select);
  RAM #(.dataWidth(16), .bus("separate")) ram_1 (
    .addr(Address), .din(data_in), .data(data_out), .str(store), .sel(1'b1), .clk(stalleable_clock),
    .ld(select), .clr(1'b0));
  Counter #(.width(4), .max('h3)) counter_1 (
    .count(or_1_out), .Q(counter_1_q), .carry(counter_1_carry), .clk(clock), .clr(clear));  // open: load, D
  Hex_Digit_Display hex_digit_display_1 (.value(counter_1_q));  // open: dp
  Multiplexer #(.disabled(0), .enable("false")) multiplexer_1 (
    .in0(clock), .in1(counter_1_carry), .out(stalleable_clock), .sel(or_1_out));
  not not_1 (Stalled, counter_1_carry);

  // Notes on the sheet:
  //   delay counter
endmodule
